# Fritzing sketch Hardware (saved by Fritzing 0.9.10b)
breadboards: 1

parts:
  Mod1 = Amica NodeMCU DEVKIT 1.0
  DHT1 = DHT11 Humitidy and Temperature Sensor (3 pins)
  LED1 = LED - 5mm [color="Red (633nm)" current=0.030 package="5 mm [THT]"]
  LED2 = LED - 5mm [color="Yellow (595nm)" current=0.030 package="5 mm [THT]"]
  M1 = 1 chan 5v relay module
  F1 = Fan - Ventilador [package=THT]
  Power_plug1 = Power plug
  XTAL1 = Crystal [frequency="16 Mhz" package=THT]

nets:
  N1: Mod1.pin1, Mod1.pin_10, Mod1.pin_26, DHT1.Plus, DHT1.Gnd
  N2: Mod1.pin2, Mod1.pin_9, Mod1.pin_25, Mod1.pin_29, LED1.cathode, LED2.cathode, M1.pin_2, F1.GND
  N3: Mod1.pin6, DHT1.Signal
  N4: Mod1.pin_12, LED2.anode
  N5: Mod1.pin_13, LED1.anode
  N6: Mod1.pin_14, M1.pin_3
  N7: Mod1.pin_30, M1.pin_1, F1.5V
  N8: M1.pin_5, Power_plug1.VCC
  N9: M1.pin_6, XTAL1.pin_0
  N10: Power_plug1.GND, XTAL1.pin_1

custom parts:
  DHT11 Humitidy and Temperature Sensor (3 pins): DHT11 Humidity and Temperature Sensor (3 pins).
  1 chan 5v relay module: 1 Channel 5V Relay Module Board Shield with Optocoupler Support High and Low Level Trigger for Arduino.
  Fan - Ventilador: Ventilador de 2 pines, se encuentra comunmente en computadoras de escritorio
